// Digital circuit MIPS.dig as structural Verilog
module MIPS (
  input  CLK
);

  wire and_1_out, and_2_out, or_1_out, or_2_out, ula_1_z;
  wire [3:0] PC_q_2;
  wire [4:0] multiplexer_1_out;
  wire [11:0] Unidade_de_Controle_d;
  wire [19:0] PC_q;
  wire [23:0] add_2_s, multiplexer_3_out, multiplexer_5_out, multiplexer_6_out;
  wire [23:2] bitextender_1_out;
  wire [31:0] bitextender_2_out, bitextender_3_out, bitextender_4_out, multiplexer_2_out, multiplexer_4_out,
       multiplexer_7_out, multiplexer_8_out, ramdualport_1_d, registradores_1_a, registradores_1_b, ula_1_s;
  wire [31:16] \Memória_de_Instrução_d , \Memória_de_Instrução_d_2 ;

  Add #(.Bits(24)) add (.a({PC_q_2, PC_q}), .b(24'h4), .c_i(1'b0));  // open: s, c_o
  Register #(.Bits(24)) PC (.D(multiplexer_6_out), .C(CLK), .en(1'b1), .Q({PC_q_2, PC_q}));
  ROM #(.AddrBits(24), .Bits(32)) \Memória_de_Instrução  (
    .A({PC_q_2, PC_q}), .sel(1'b1), .D({\Memória_de_Instrução_d_2 , \Memória_de_Instrução_d }));
  ROM #(.AddrBits(5), .Bits(12)) Unidade_de_Controle (
    .A(\Memória_de_Instrução_d_2 [30:26]), .sel(1'b1), .D(Unidade_de_Controle_d));
  BitExtender #(.inputBits(16), .outputBits(22)) bitextender_1 (.in(\Memória_de_Instrução_d ), .out(bitextender_1_out));
  Multiplexer #(.Bits(5)) multiplexer_1 (
    .sel(Unidade_de_Controle_d[5]), .in_0(\Memória_de_Instrução_d [31:27]),
    .in_1(\Memória_de_Instrução_d_2 [20:16]), .out(multiplexer_1_out));
  Add #(.Bits(24)) add_2 (.a({PC_q_2, PC_q}), .b(24'h1), .c_i(1'b0), .s(add_2_s));  // open: c_o
  BitExtender #(.inputBits(24), .outputBits(32)) bitextender_2 (.in(add_2_s), .out(bitextender_2_out));
  BitExtender #(.inputBits(16), .outputBits(32)) bitextender_3 (.in(\Memória_de_Instrução_d ), .out(bitextender_3_out));
  BitExtender #(.inputBits(16), .outputBits(32)) bitextender_4 (.in(\Memória_de_Instrução_d ), .out(bitextender_4_out));
  registradores registradores_1 (
    .D(multiplexer_8_out), .clk(CLK), .write_enable(Unidade_de_Controle_d[11]),
    .write_register(multiplexer_1_out), .RA(\Memória_de_Instrução_d_2 [25:21]),
    .RB(\Memória_de_Instrução_d_2 [20:16]), .R31_IN(bitextender_2_out), .LINK(Unidade_de_Controle_d[0]),
    .A(registradores_1_a), .B(registradores_1_b));
  Multiplexer #(.Bits(32)) multiplexer_2 (
    .sel(Unidade_de_Controle_d[2]), .in_0(bitextender_3_out), .in_1(bitextender_4_out),
    .out(multiplexer_2_out));
  Multiplexer #(.Bits(24)) multiplexer_3 (
    .sel(Unidade_de_Controle_d[0]), .in_0(registradores_1_a[23:0]),
    .in_1({\Memória_de_Instrução_d_2 [21:16], \Memória_de_Instrução_d , 2'b00}), .out(multiplexer_3_out));
  Multiplexer #(.Bits(32)) multiplexer_4 (
    .sel(Unidade_de_Controle_d[5]), .in_0(registradores_1_b), .in_1(multiplexer_2_out),
    .out(multiplexer_4_out));
  and and_1 (and_1_out, Unidade_de_Controle_d[4], ula_1_z);
  ULA ula_1 (
    .A(registradores_1_a), .B(multiplexer_4_out), .OP(Unidade_de_Controle_d[10:8]),
    .shamt(\Memória_de_Instrução_d [26:22]), .S(ula_1_s), .Z(ula_1_z));
  // Probe on ula_1_s
  Multiplexer #(.Bits(24)) multiplexer_5 (
    .sel(or_1_out), .in_0(multiplexer_3_out), .in_1({bitextender_1_out, 2'b00}), .out(multiplexer_5_out));
  or or_1 (or_1_out, and_1_out, and_2_out);
  and and_2 (and_2_out, Unidade_de_Controle_d[4], ~ula_1_z);  // And
  RAMDualPort #(.AddrBits(24), .Bits(32)) ramdualport_1 (
    .A(ula_1_s[23:0]), .Din(registradores_1_b), .str(Unidade_de_Controle_d[7]), .C(CLK),
    .ld(Unidade_de_Controle_d[6]), .D(ramdualport_1_d));
  Multiplexer #(.Bits(24)) multiplexer_6 (
    .sel(or_2_out), .in_0({PC_q_2, PC_q}), .in_1(multiplexer_5_out), .out(multiplexer_6_out));
  or or_2 (or_2_out, Unidade_de_Controle_d[3], Unidade_de_Controle_d[4]);
  // Probe on ramdualport_1_d
  Multiplexer #(.Bits(32)) multiplexer_7 (
    .sel(Unidade_de_Controle_d[6]), .in_0(ula_1_s), .in_1(ramdualport_1_d), .out(multiplexer_7_out));
  Multiplexer #(.Bits(32)) multiplexer_8 (
    .sel(Unidade_de_Controle_d[1]), .in_0(multiplexer_7_out), .in_1({\Memória_de_Instrução_d , {16{1'b0}}}),
    .out(multiplexer_8_out));

  // Notes on the sheet:
  //   contents of Memória_de_Instrução (hex, n*v repeats v):
  //   4010,4200,201,8222,c810,14810,200,49f0,201f0,b31c,c394,34e50,38a64
  //   ,3cc90,4ce80,48ca0,292a0,24090,40a30,44b14,1c000,4000,1f07,5ab0
  //   ,1ae7,4c6f0,10610,4210,18000
  //   formatos de instrução
  //   contents of Unidade_de_Controle (hex, n*v repeats v):
  //   800,820,a00,a24,110,110,8,809,8,842,860,c00,b00,b24,d00,d20,e00
  //   ,f00,a0,900
  //   PC + 4
  //   controles
  //   "And imm" e "imm"
  //   com sinal
  //   sem sinal
  //   JumpAddr
  //   branches
  //   BranchAdder
  //   Memória de Dados
  //   "imm" não estendido
  //   "lui"
endmodule
