// Digital circuit ULA.dig as structural Verilog
module ULA (
  input  [31:0] A,
  input  [31:0] B,
  input  [2:0] OP,
  output [31:0] S,
  output [31:0] Z
);

  wire [0:0] comparator_lt;
  wire [31:0] add_s, and_1_out, or_1_out, shift_left_out, shift_right_out, sub_s;

  Add #(.Bits(32)) add (.a(A), .b(B), .c_i(1'b0), .s(add_s));  // open: c_o
  Sub #(.Bits(32)) sub (.a(A), .b(B), .c_i(1'b0), .s(sub_s));  // open: c_o
  assign and_1_out = A & B;  // And and_1, 32 bits wide
  assign or_1_out = A | B;  // Or or_1, 32 bits wide
  Comparator #(.Bits(32)) comparator (.a(A), .b(B), .eq(Z[0]), .lt(comparator_lt[0]));  // open: gt
  BarrelShifter #(.Bits(32)) shift_left (.in(A), .shift({1'b0, B[4:0]}), .out(shift_left_out));
  BarrelShifter #(.Bits(32), .direction("right")) shift_right (.in(A), .shift({1'b0, B[4:0]}), .out(shift_right_out));
  Multiplexer #(.Selector_Bits(3), .Bits(32)) multiplexer_1 (
    .sel(OP), .in_0(add_s), .in_1(sub_s), .in_2(and_1_out), .in_3(or_1_out), .in_4({{31{1'b0}}, Z[0]}),
    .in_5({{31{1'b0}}, comparator_lt[0]}), .in_6(shift_left_out), .in_7(shift_right_out), .out(S));
  // Pins of 1 and 32 bits meet at {{31{1'b0}}, Z[0]}

  assign Z[31:1] = {31{1'b0}};
endmodule
